# Fritzing sketch OpenMV Camera Release (saved by Fritzing 0.9.10b)

parts:
  U5 = 2.5mm Audio Jack [package=stereojack2.5mm_specia_pogopins]
  U6 = OpenMV3
  U1 = Sharp PC817 [package=THT]

nets:
  N1: U5.SLEEVE, U1.Pin_3
  N2: U5.LEFT, U5.RIGHT, U1.Pin_4
  N3: U6.P0/MOSI, U1.Pin_1
  N4: U6.GND, U1.Pin_2

notes:
  Camera Adapter
  Mini Jack (2.5mm)
  optocoupler collector going to right and left and emiter going to the sleeve of the minijack
  we use a 4n25 optocoupler to isolate the circuit from the main cameras elctronics

custom parts:
  OpenMV3: OpenMV Cam
